# Fritzing sketch circuitdesignFPGA (saved by Fritzing 0.9.4)
breadboards: 4

parts:
  U1 = OP27 - Low Noise, Precision Op Amp [part_number=MCP6002]
  R1 = Resistor [tolerance=±5% resistance=18k package=THT]
  R2 = Resistor [tolerance=±5% resistance=33k package=THT]
  R3 = Resistor [tolerance=±5% resistance=18k package=THT]
  R4 = Resistor [tolerance=±5% resistance=33k package=THT]
  U2 = OP27 - Low Noise, Precision Op Amp [part_number=MCP6002]
  R5 = Resistor [tolerance=±5% resistance=18k package=THT]
  R6 = Resistor [tolerance=±5% resistance=18k package=THT]
  R7 = Resistor [tolerance=±5% resistance=33k package=THT]
  R8 = Resistor [tolerance=±5% resistance=33k package=THT]
  U3 = POT [package=alps_pot]
  RE1 = Rotary Encoder [package=THT]
  RE3 = Rotary Encoder [package=THT]
  U4 = POT [package=alps_pot]
  U5 = POT [package=alps_pot]
  U6 = POT [package=alps_pot]
  RE4 = Rotary Encoder [package=THT]
  RE5 = Rotary Encoder [package=THT]
  RE6 = Rotary Encoder [package=THT]
  RE7 = Rotary Encoder [package=THT]
  S1 = Toggle Switch [package=THT]
  U7 = OP27 - Low Noise, Precision Op Amp [part_number=MCP6002]

nets:
  N1: U1.TRIM#1, U1.-IN, R1.Pin_0
  N2: U1.-V, R2.Pin_0, R4.Pin_1, U5.A, U6.A, RE4.EncoderPinB, RE5.EncoderPinB, RE6.EncoderPinB, RE7.EncoderPinB, U7.-V
  N3: U1.NC, U1.TRIM#8, U7.TRIM#8
  N4: U1.OUT, U1.V+, R3.Pin_1
  N5: R1.Pin_1, R2.Pin_1
  N6: R3.Pin_0, R4.Pin_0, U5.E, U6.E, RE4.EncoderPinA, RE5.EncoderPinA, RE6.EncoderPinA, RE7.EncoderPinA, S1.L1
  N7: U2.TRIM#1, U2.-IN, R5.Pin_0
  N8: U2.-V, R7.Pin_0, R8.Pin_1, U3.A, RE1.EncoderPinB, RE3.EncoderPinB, U4.A
  N9: U2.NC, U2.TRIM#8
  N10: U2.OUT, U2.V+, R6.Pin_1
  N11: R5.Pin_1, R7.Pin_1
  N12: R6.Pin_0, R8.Pin_0, U3.E, RE1.EncoderPinA, RE3.EncoderPinA, U4.E

notes:
  5V VDD
  from pin 5V0
  0V Vss
  Vout from the Probe on conductive paper
  V0 the output to port A0
  3.3V DC for knobs
  5V VDD
  Vout from the Probe
  V3 V4 V5 V6 controls theta, phi, zoom and Z scale
  Mode 1 and 2 for real and wave simulation
  knobs control theta, phi, zoom, Z scale, magnitude
